// Logisim project Shmerlard8.circ as structural Verilog: 21 circuits, main circuit main
module main (
  input  RST,
  input  [15:0] in_2,
  input  MAN,
  input  MANUAL_CONTROL,
  input  in_5,
  input  in_6,
  input  in_7,
  input  in_8,
  input  in_9,
  input  in_10,
  input  in_11,
  input  in_12,
  input  in_13,
  input  in_14,
  input  [3:0] in_15,
  input  in_16,
  input  in_17,
  input  in_18,
  input  in_19,
  input  in_20,
  input  in_21,
  input  in_22,
  input  in_23,
  input  in_24,
  input  in_25,
  input  [15:0] IN_REG,
  output [3:0] OPCODE,
  output [3:0] TC_T,
  output [2:0] IR_ADD_MODE,
  output CON,
  output SC_N_EQ_0
);

  wire CLK, CLK_out, CON_in, DSTsel, extra_alu_input_1_c_en, extra_alu_input_1_cyc_en, extra_alu_input_1_m,
       extra_alu_input_1_sh_en, GOTO6, HLT, IR_IN, MAR_IN, MDR_EN, MEM_SEL, memory_registers_1_ram_out_en,
       memory_registers_1_ram_wr_en, not_1_out, PC_IN, PC_INC, PC_OUT, RF_IN, RF_OUT, ROM_EN, SC_DEC, SC_LD,
       TC_END, V_OUT, WR_SEL, X_IN, Y_IN, Y_OUT;
  wire [3:0] ALU_CTRL, extra_alu_input_1_s, FLAGS_CON, instruction_register_1_reg_sel_dst,
       instruction_register_1_reg_sel_src, z74_alu_1_flags_out;
  wire [14:0] ADDRESS_BUS;
  wire [15:0] MANUAL, MEM_DATA, register_file_1_out_reg, rom_1_data;
  wire [15:15] memory_registers_1_mem_address_out;

  assign PC_IN = MANUAL_CONTROL ? in_5 : 1'bz;  // Controlled_Buffer controlled_buffer_1
  assign RF_IN = MANUAL_CONTROL ? in_16 : 1'bz;  // Controlled_Buffer controlled_buffer_2
  assign IR_IN = MANUAL_CONTROL ? in_24 : 1'bz;  // Controlled_Buffer controlled_buffer_3
  assign PC_OUT = MANUAL_CONTROL ? in_8 : 1'bz;  // Controlled_Buffer controlled_buffer_4
  assign PC_INC = MANUAL_CONTROL ? in_11 : 1'bz;  // Controlled_Buffer controlled_buffer_5
  assign RF_OUT = MANUAL_CONTROL ? in_19 : 1'bz;  // Controlled_Buffer controlled_buffer_6
  assign DSTsel = MANUAL_CONTROL ? in_21 : 1'bz;  // Controlled_Buffer controlled_buffer_7
  assign V_OUT = MANUAL_CONTROL ? in_25 : 1'bz;  // Controlled_Buffer controlled_buffer_8
  not not_1 (not_1_out, HLT);
  Clock u_CLK (.out(CLK_out));
  assign MAR_IN = MANUAL_CONTROL ? in_6 : 1'bz;  // Controlled_Buffer controlled_buffer_9
  assign TC_END = MANUAL_CONTROL ? in_17 : 1'bz;  // Controlled_Buffer controlled_buffer_10
  and and_1 (CLK, not_1_out, CLK_out);
  assign MANUAL = MAN ? in_2 : 16'bz;  // Controlled_Buffer controlled_buffer_11
  assign MDR_EN = MANUAL_CONTROL ? in_9 : 1'bz;  // Controlled_Buffer controlled_buffer_12
  assign WR_SEL = MANUAL_CONTROL ? in_12 : 1'bz;  // Controlled_Buffer controlled_buffer_13
  assign MEM_SEL = MANUAL_CONTROL ? in_14 : 1'bz;  // Controlled_Buffer controlled_buffer_14
  assign GOTO6 = MANUAL_CONTROL ? in_20 : 1'bz;  // Controlled_Buffer controlled_buffer_15
  // Probe on register_file_1_out_reg
  assign X_IN = MANUAL_CONTROL ? in_7 : 1'bz;  // Controlled_Buffer controlled_buffer_16
  assign Y_IN = MANUAL_CONTROL ? in_10 : 1'bz;  // Controlled_Buffer controlled_buffer_17
  assign Y_OUT = MANUAL_CONTROL ? in_13 : 1'bz;  // Controlled_Buffer controlled_buffer_18
  assign ALU_CTRL = MANUAL_CONTROL ? in_15 : 4'bz;  // Controlled_Buffer controlled_buffer_19
  assign CON_in = MANUAL_CONTROL ? in_18 : 1'bz;  // Controlled_Buffer controlled_buffer_20
  assign SC_LD = MANUAL_CONTROL ? in_22 : 1'bz;  // Controlled_Buffer controlled_buffer_21
  assign SC_DEC = MANUAL_CONTROL ? in_23 : 1'bz;  // Controlled_Buffer controlled_buffer_22
  // Probe on FLAGS_CON
  extra_alu_input extra_alu_input_1 (
    .Input(ALU_CTRL), .M(extra_alu_input_1_m), .C_EN(extra_alu_input_1_c_en),
    .SH_EN(extra_alu_input_1_sh_en), .CYC_EN(extra_alu_input_1_cyc_en), .S(extra_alu_input_1_s));
  // Probe on IR_ADD_MODE
  // Probe on instruction_register_1_reg_sel_src
  // Probe on instruction_register_1_reg_sel_dst
  program_counter program_counter_1 (
    .CLK(CLK), .RST(RST), .PC_OUT(PC_OUT), .PC_IN(PC_IN), .PC_INC(PC_INC), .D_BUS(MANUAL), .D_BUS_OUT(MANUAL));
  instruction_register instruction_register_1 (
    .CLK(CLK), .V_out(V_OUT), .D_BUS(MANUAL), .IR_WR_EN(IR_IN), .RST(RST),
    .REG_SEL_DST(instruction_register_1_reg_sel_dst), .ADDR_MODE(IR_ADD_MODE),
    .REG_SEL_SRC(instruction_register_1_reg_sel_src), .OP_CODE(OPCODE), .D_BUS_OUT(MANUAL));
  register_file register_file_1 (
    .IN_REG(IN_REG), .DST_SEL(DSTsel), .RF_IN(RF_IN), .REG_RD(RF_OUT), .FLAGS_IN(z74_alu_1_flags_out),
    .RF_FL_IN(Y_IN), .REG_SEL_SRC(instruction_register_1_reg_sel_src),
    .REG_SEL_DST(instruction_register_1_reg_sel_dst), .CLK(CLK), .RST(RST), .DATA_IN(MANUAL),
    .OUT_REG(register_file_1_out_reg), .DATA_OUT(MANUAL), .FLAGS_OUT(FLAGS_CON), .HLT(HLT));
  z74_alu z74_alu_1 (
    .Y_OUT(Y_OUT), .Y_IN(Y_IN), .X_in(X_IN), .RST(RST), .CLK(CLK), .S_in(extra_alu_input_1_s),
    .M_in(extra_alu_input_1_m), .ALU_Carry_En(extra_alu_input_1_c_en), .SH_EN(extra_alu_input_1_sh_en),
    .CYC_EN(extra_alu_input_1_cyc_en), .Flags_in(FLAGS_CON), .DATAIN(MANUAL),
    .FLAGS_OUT(z74_alu_1_flags_out), .Y_DATA_OUT(MANUAL));  // open: A_EQ_B
  // Probe on MANUAL
  condition_control condition_control_1 (
    .CON_SEL(MANUAL[2:0]), .Flags_in(FLAGS_CON), .RST(RST), .CLK(CLK), .CON_in(CON_in), .CON(CON));
  memory_registers memory_registers_1 (
    .D_BUS(MANUAL), .MAR_WR_EN(MAR_IN), .CLK(CLK), .RST(RST), .MDR_EN(MDR_EN), .WR_SEL(WR_SEL),
    .MEM_SEL(MEM_SEL), .MEM_DATA_IN(MEM_DATA), .D_BUS_OUT(MANUAL), .MEM_DATA_OUT(MEM_DATA),
    .RAM_WR_EN(memory_registers_1_ram_wr_en), .RAM_OUT_EN(memory_registers_1_ram_out_en),
    .ROM_OUT_EN(ROM_EN), .MEM_ADDRESS_OUT({memory_registers_1_mem_address_out[15], ADDRESS_BUS}));
  timing_control TIME_CONTROL (.CLK(CLK), .RST(RST), .GOTO6(GOTO6), .TC_END(TC_END), .T_OUT(TC_T));
  shift_control shift_control_1 (
    .CLK(CLK), .RST(RST), .SHC_IN(SC_LD), .SHC_DEC(SC_DEC), .D_IN(MANUAL), .SHC_EQ0(SC_N_EQ_0));
  control_logic control_logic_1 (
    .CON(CON), .N_EQ_0(SC_N_EQ_0), .ADDRESSING_MODE(IR_ADD_MODE), .OPCODE(OPCODE), .T_TIME(TC_T),
    .MANUAL_CONTROL(MANUAL_CONTROL), .CONin(CON_in), .PC({PC_INC, PC_OUT, PC_IN}),
    .RF({DSTsel, RF_OUT, RF_IN}), .IR({V_OUT, IR_IN}), .ALU(ALU_CTRL), .XY({Y_OUT, Y_IN, X_IN}),
    .MEM_REGISTERS({MEM_SEL, WR_SEL, MDR_EN, MAR_IN}), .TC({GOTO6, TC_END}), .SC({SC_DEC, SC_LD}));
  // Probe on ALU_CTRL
  ROM #(.addrWidth(15), .dataWidth(16)) rom_1 (.addr(ADDRESS_BUS), .data(rom_1_data));
  RAM #(.addrWidth(15), .asyncread("true"), .dataWidth(16), .databus("bidir")) ram_1 (
    .addr(ADDRESS_BUS), .we(memory_registers_1_ram_wr_en), .oe(memory_registers_1_ram_out_en), .clk(CLK),
    .data(MEM_DATA));
  assign MEM_DATA = ROM_EN ? rom_1_data : 16'bz;  // Controlled_Buffer controlled_buffer_23

  // Other names for the same wires on the sheet: ADDR_MODE[2:0] = IR_ADD_MODE

  // Notes on the sheet:
  //   ENZC
  //   contents of rom_1 (hex, n*v repeats v):
  //   25 fa1c c025 ffff
endmodule

module alu (
  input  CLK,
  input  RST,
  input  [15:0] D_BUS,
  input  X_IN,
  input  ADD_CARRY,
  input  [2:0] ALU_MUX,
  input  [3:0] FL_IN_ONZC,
  input  Y_IN,
  input  Y_OUT,
  output [3:0] FL_OUT,
  output [15:0] D_BUS_OUT
);

  wire and_2_out, C_OUT;
  wire [15:0] multiplexer_1_out, undriven, X1, Y_ADD, Y_AND, Y_EQ_B, Y_NOT, Y_OR, Y_REG_q, Y_SHRA, Y_SHRC,
       Y_SUB, Y_XOR;

  Register #(.width(16)) X_REG (.D(D_BUS), .en(X_IN), .clk(CLK), .Q(X1), .clr(RST));
  // Probe on Y_AND
  assign Y_AND = D_BUS & X1;  // AND_Gate and_1, 16 bits wide
  // Probe on Y_XOR
  assign Y_XOR = D_BUS ^ X1;  // XOR_Gate xor_1, 16 bits wide
  // Probe on Y_OR
  assign Y_OR = D_BUS | X1;  // OR_Gate or_1, 16 bits wide
  // Probe on Y_SUB
  Subtractor #(.width(16)) subtractor_1 (.a(D_BUS), .b(X1), .out(Y_SUB));  // open: bin, bout
  and and_2 (and_2_out, ADD_CARRY, FL_IN_ONZC[0]);
  // Probe on Y_ADD
  Adder #(.width(16)) adder_1 (.a(D_BUS), .b(X1), .out(Y_ADD), .cin(and_2_out), .cout(C_OUT));
  Multiplexer #(.select(3), .width(16)) multiplexer_1 (
    .in0(Y_ADD), .in1(Y_SUB), .in2(Y_AND), .in3(Y_OR), .in4(Y_XOR), .in5(Y_NOT), .in6(Y_EQ_B),
    .in7(undriven), .out(multiplexer_1_out));  // open: sel
  // Probe on Y_SHRA
  Shifter #(.shift("lr"), .width(16)) shifter_1 (.in(D_BUS), .\dist (4'b0001), .out(Y_SHRA));
  // Probe on Y_SHRC
  Shifter #(.shift("rr"), .width(16)) shifter_2 (.in(D_BUS), .\dist (4'b0001), .out(Y_SHRC));
  assign D_BUS_OUT = Y_OUT ? Y_REG_q : 16'bz;  // Controlled_Buffer controlled_buffer_1
  Register #(.width(16)) Y_REG (.D(multiplexer_1_out), .en(Y_IN), .clk(CLK), .Q(Y_REG_q), .clr(RST));

  // Other names for the same wires on the sheet: C_FLAG = FL_IN_ONZC[0]; Z_FLAG = FL_IN_ONZC[1];
  //   N_FLAG = FL_IN_ONZC[2]; O_FLAG = FL_IN_ONZC[3]; X2[15:0] = D_BUS
endmodule

module condition_control (
  input  [2:0] CON_SEL,
  input  RST,
  input  CLK,
  input  CON_in,
  input  [3:0] Flags_in,
  output CON
);

  wire and_3_out, and_4_out, and_5_out, and_6_out, and_7_out, and_8_out, CON_0_NVR, CON_1_JH, CON_2_JEQ,
       CON_3_JHS, CON_4_JL, CON_5_JNE, CON_6_JLS, CON_7_JMP, JH, JL, not_1_out, not_2_out, not_3_out,
       not_4_out, or_1_out, or_2_out, or_3_out, or_4_out, or_5_out, or_6_out;

  not not_1 (not_1_out, Flags_in[1]);
  not not_2 (not_2_out, Flags_in[0]);
  and and_1 (JH, Flags_in[0], not_1_out);
  and and_2 (JL, not_1_out, not_2_out);
  not not_3 (not_3_out, Flags_in[1]);
  not not_4 (not_4_out, Flags_in[0]);
  and and_3 (and_3_out, CON_1_JH, JH);
  and and_4 (and_4_out, CON_2_JEQ, Flags_in[1]);
  and and_5 (and_5_out, CON_3_JHS, Flags_in[0]);
  and and_6 (and_6_out, CON_4_JL, JL);
  and and_7 (and_7_out, CON_5_JNE, not_3_out);
  and and_8 (and_8_out, CON_6_JLS, not_4_out);
  or or_1 (or_1_out, and_3_out, and_4_out);
  or or_2 (or_2_out, and_5_out, and_6_out);
  or or_3 (or_3_out, and_7_out, and_8_out);
  or or_4 (or_4_out, or_1_out, or_2_out);
  or or_5 (or_5_out, or_3_out, CON_7_JMP);
  Decoder #(.enable("false"), .select(3)) decoder_1 (
    .out0(CON_0_NVR), .out1(CON_1_JH), .out2(CON_2_JEQ), .out3(CON_3_JHS), .out4(CON_4_JL), .out5(CON_5_JNE),
    .out6(CON_6_JLS), .out7(CON_7_JMP), .sel(CON_SEL));
  or or_6 (or_6_out, or_4_out, or_5_out);
  D_Flip_Flop #(.trigger("high")) d_ff_1 (.D(or_6_out), .clk(CON_in), .Q(CON), .reset(RST));  // open: Qn, preset

  // Other names for the same wires on the sheet: C_F = Flags_in[0]; Z_F = Flags_in[1]; N_F = Flags_in[2];
  //   E_F = Flags_in[3]
endmodule

module control_logic (
  input  MANUAL_CONTROL,
  input  CON,
  input  N_EQ_0,
  input  [2:0] ADDRESSING_MODE,
  input  [3:0] OPCODE,
  input  [3:0] T_TIME,
  output [2:0] PC,
  output [2:0] RF,
  output [1:0] IR,
  output [3:0] MEM_REGISTERS,
  output [1:0] TC,
  output [1:0] SC,
  output [2:0] XY,
  output [3:0] ALU,
  output CONin
);

  wire not_1_out;
  wire [7:0] EEPROM0_data, EEPROM1_data, EEPROM2_data;

  ROM #(.addrWidth(15)) EEPROM0 (.addr({2'b00, CON, N_EQ_0, ADDRESSING_MODE, OPCODE, T_TIME}), .data(EEPROM0_data));
  ROM #(.addrWidth(15)) EEPROM1 (.addr({2'b00, CON, N_EQ_0, ADDRESSING_MODE, OPCODE, T_TIME}), .data(EEPROM1_data));
  ROM #(.addrWidth(15)) EEPROM2 (.addr({2'b00, CON, N_EQ_0, ADDRESSING_MODE, OPCODE, T_TIME}), .data(EEPROM2_data));
  not not_1 (not_1_out, MANUAL_CONTROL);
  assign {IR, RF, PC} = not_1_out ? EEPROM0_data : 8'bz;  // Controlled_Buffer controlled_buffer_1
  assign {SC, TC, MEM_REGISTERS} = not_1_out ? EEPROM1_data : 8'bz;  // Controlled_Buffer controlled_buffer_2
  assign {CONin, ALU, XY} = not_1_out ? EEPROM2_data : 8'bz;  // Controlled_Buffer controlled_buffer_3

  // Notes on the sheet:
  //   contents of EEPROM0 (hex, n*v repeats v):
  //   6 0 40 10 28 11*0 6 0 40 13*0 6 0 40 30 10 28 10*0 6 0 40 10 8 0 28 9*0 6 0 40 10 30 28 10*0 6 0 40
  //   13*0 6 0 40 10 30 28 10*0 6 0 40 10 30 11*0 6 0 40 10 30 0 0 28 8*0 6 0 40 13*0 6 0 40 10 30 28 10*0
  //   6 0 40 10 30 28 10*0 6 0 40 10 30 28 10*0 6 0 40 13*0 6 0 40 2 10 8 31 9*0 6 0 40 80 12*0 6 0 40 10
  //   0 28 10*0 6 0 40 30 10 11*0 6 0 40 13*0 6 0 40 13*0 6 0 40 10 30 0 28 9*0 6 0 40 13*0 6 0 40 13*0 6
  //   0 40 13*0 6 0 40 13*0 6 0 40 13*0 6 0 40 6 30 0 28 9*0 6 0 40 6 30 0 28 9*0 6 0 40 6 30 0 28 9*0 6 0
  //   40 13*0 6 0 40 13*0 6 0 40 13*0 6 0 40 6 0 28 10*0 6 0 40 13*0 6 0 40 6 0 30 28 9*0 6 0 40 13*0 6 0
  //   40 6 30 0 28 9*0 6 0 40 13*0 6 0 40 6 0 0 0 28 8*0 6 0 40 6 12*0 6 0 40 6 30 11*0 6 0 40 13*0 6 0 40
  //   6 30 0 28 9*0 6 0 40 6 30 0 28 9*0 6 0 40 6 30 0 28 9*0 6 0 40 13*0 6 0 40 6 0 0 2 1 10 8 6*0 6 0 40
  //   6 80 11*0 6 0 40 6 0 0 0 28 8*0 6 0 40 13*0 6 0 40 13*0 6 0 40 10 8 0 1 9*0 6 0 40 13*0 6 0 40 13*0
  //   6 0 40 13*0 6 0 40 13*0 6 0 40 13*0 6 0 40 13*0 6 0 40 6 30 0 0 0 28 7*0 6 0 40 6 30 0 0 0 28 7*0 6
  //   0 40 6 30 0 0 0 28 7*0 6 0 40 13*0 6 0 40 13*0 6 0 40 13*0 6 0 40 13*0 6 0 40 13*0 6 0 40 13*0 6 0
  //   40 13*0 6 0 40 13*0 6 0 40 13*0 6 0 40 13*0 6 0 40 13*0 6 0 40 13*0 6 0 40 13*0 6 0 40 13*0 6 0 40
  //   13*0 6 0 40 13*0 6 0 40 13*0 6 0 40 13*0 6 0 40 13*0 6 0 40 13*0 6 0 40 13*0 6 0 40 13*0 6 0 40 13*0
  //   6 0 40 13*0 6 0 40 13*0 6 0 40 13*0 6 0 40 13*0 6 0 40 13*0 6 0 40 13*0 6 0 40 13*0 6 0 40 13*0 6 0
  //   40 13*0 6 0 40 13*0 6 0 40 13*0 6 0 40 13*0 6 0 40 13*0 6 0 40 13*0 6 0 40 13*0 6 0 40 13*0 6 0 40
  //   13*0 6 0 40 13*0 6 0 40 13*0 6 0 40 13*0 6 0 40 13*0 6 0 40 13*0 6 0 40 13*0 6 0 40 13*0 6 0 40 13*0
  //   6 0 40 13*0 6 0 40 13*0 6 0 40 13*0 6 0 40 13*0 6 0 40 13*0 6 0 40 13*0 6 0 40 13*0 6 0 40 13*0 6 0
  //   40 13*0 6 0 40 13*0 6 0 40 13*0 6 0 40 13*0 6 0 40 13*0 6 0 40 13*0 6 0 40 13*0 6 0 40 13*0 6 0 40
  //   13*0 6 0 40 13*0 6 0 40 13*0 6 0 40 10 28 11*0 6 0 40 13*0 6 0 40 30 10 28 10*0 6 0 40 10 8 0 28 9*0
  //   6 0 40 10 30 28 10*0 6 0 40 13*0 6 0 40 10 30 28 10*0 6 0 40 10 30 11*0 6 0 40 10 30 0 28 28 8*0 6 0
  //   40 13*0 6 0 40 10 30 28 10*0 6 0 40 10 30 28 10*0 6 0 40 10 30 28 10*0 6 0 40 13*0 6 0 40 2 10 8 31
  //   9*0 6 0 40 80 12*0 6 0 40 10 0 28 10*0 6 0 40 30 10 11*0 6 0 40 13*0 6 0 40 13*0 6 0 40 10 30 0 28
  //   9*0 6 0 40 13*0 6 0 40 13*0 6 0 40 13*0 6 0 40 13*0 6 0 40 13*0 6 0 40 6 30 0 28 9*0 6 0 40 6 30 0
  //   28 9*0 6 0 40 6 30 0 28 9*0 6 0 40 13*0 6 0 40 13*0 6 0 40 13*0 6 0 40 6 0 28 10*0 6 0 40 13*0 6 0
  //   40 6 0 30 28 9*0 6 0 40 13*0 6 0 40 6 30 0 28 9*0 6 0 40 13*0 6 0 40 6 0 0 0 28 8*0 6 0 40 6 12*0 6
  //   0 40 6 30 0 28 9*0 6 0 40 13*0 6 0 40 6 30 0 28 9*0 6 0 40 6 30 0 28 9*0 6 0 40 6 30 0 28 9*0 6 0 40
  //   13*0 6 0 40 6 0 0 2 1 10 8 6*0 6 0 40 6 80 11*0 6 0 40 6 0 0 0 28 8*0 6 0 40 13*0 6 0 40 13*0 6 0 40
  //   10 8 0 1 9*0 6 0 40 13*0 6 0 40 13*0 6 0 40 13*0 6 0 40 13*0 6 0 40 13*0 6 0 40 13*0 6 0 40 6 30 0 0
  //   0 28 7*0 6 0 40 6 30 0 0 0 28 7*0 6 0 40 6 30 0 0 0 28 7*0 6 0 40 13*0 6 0 40 13*0 6 0 40 13*0 6 0
  //   40 13*0 6 0 40 13*0 6 0 40 13*0 6 0 40 13*0 6 0 40 13*0 6 0 40 13*0 6 0 40 13*0 6 0 40 13*0 6 0 40
  //   13*0 6 0 40 13*0 6 0 40 13*0 6 0 40 13*0 6 0 40 13*0 6 0 40 13*0 6 0 40 13*0 6 0 40 13*0 6 0 40 13*0
  //   6 0 40 13*0 6 0 40 13*0 6 0 40 13*0 6 0 40 13*0 6 0 40 13*0 6 0 40 13*0 6 0 40 13*0 6 0 40 13*0 6 0
  //   40 13*0 6 0 40 13*0 6 0 40 13*0 6 0 40 13*0 6 0 40 13*0 6 0 40 13*0 6 0 40 13*0 6 0 40 13*0 6 0 40
  //   13*0 6 0 40 13*0 6 0 40 13*0 6 0 40 13*0 6 0 40 13*0 6 0 40 13*0 6 0 40 13*0 6 0 40 13*0 6 0 40 13*0
  //   6 0 40 13*0 6 0 40 13*0 6 0 40 13*0 6 0 40 13*0 6 0 40 13*0 6 0 40 13*0 6 0 40 13*0 6 0 40 13*0 6 0
  //   40 13*0 6 0 40 13*0 6 0 40 13*0 6 0 40 13*0 6 0 40 13*0 6 0 40 13*0 6 0 40 13*0 6 0 40 13*0 6 0 40
  //   13*0 6 0 40 13*0 6 0 40 13*0 6 0 40 13*0 6 0 40 13*0 6 0 40 13*0 6 0 40 10 28 11*0 6 0 40 13*0 6 0
  //   40 30 10 28 10*0 6 0 40 10 8 0 28 9*0 6 0 40 10 30 28 10*0 6 0 40 13*0 6 0 40 10 30 28 10*0 6 0 40
  //   10 30 11*0 6 0 40 10 30 0 0 28 8*0 6 0 40 13*0 6 0 40 10 30 28 10*0 6 0 40 10 30 28 10*0 6 0 40 10
  //   30 28 10*0 6 0 40 13*0 6 0 40 2 10 8 31 9*0 6 0 40 80 11 11*0 6 0 40 10 0 28 10*0 6 0 40 30 10 11*0
  //   6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
  //   contents of EEPROM1 (hex, n*v repeats v):
  //   1 a 6 0 0 10 10*0 1 a 6 10 10 10 10*0 1 a 6 1 2 e 10 9*0 1 a 6 0 1 a 6 10 8*0 1 a 6 0 0 0 10 9*0 1 a
  //   6 4*10 9*0 1 a 6 0 0 0 10 9*0 1 a 6 0 0 10 10*0 1 a 6 40 0 0 a0 9*0 1 a 6 4*10 9*0 1 a 6 0 0 0 10
  //   9*0 1 a 6 0 0 0 10 9*0 1 a 6 0 0 0 10 9*0 1 a 6 13*0 1 a 6 2 1 e 0 10 8*0 1 a 6 0 10 10 10*0 1 a 6 1
  //   a 6 10 9*0 1 a 6 1 2 e 10 9*0 1 a 6 5*10 8*0 1 a 6 5*10 8*0 1 a 6 1 a 6 0 10 8*0 1 a 6 4*10 9*0 1 a
  //   6 4*10 9*0 1 a 6 5*10 8*0 1 a 6 4*10 9*0 1 a 6 4*10 9*0 1 a 6 1 a 6 0 10 8*0 1 a 6 1 a 6 0 10 8*0 1
  //   a 6 1 a 6 0 10 8*0 1 a 6 13*0 1 a 6 4*10 9*0 1 a 6 4*10 9*0 1 a 6 1 a 6 10 9*0 1 a 6 10 10 10 10*0 1
  //   a 6 1 a 1 e 10 8*0 1 a 6 5*10 8*0 1 a 6 1 a 6 0 10 8*0 1 a 6 4*10 9*0 1 a 6 1 a 6 0 0 10 7*0 1 a 6 1
  //   a 6 0 10 8*0 1 a 6 1 a 46 a0 10 8*0 1 a 6 4*10 9*0 1 a 6 1 a 6 0 10 8*0 1 a 6 1 a 6 0 10 8*0 1 a 6 1
  //   a 6 0 10 8*0 1 a 6 13*0 1 a 6 1 a 6 2 0 1 e 10 5*0 1 a 6 1 a 10 10 9*0 1 a 6 1 a 7 a 6 10 7*0 1 a 6
  //   10 10 10 10*0 1 a 6 5*10 8*0 1 a 6 0 1 a 6 10 8*0 1 a 6 5*10 8*0 1 a 6 4*10 9*0 1 a 6 6*10 7*0 1 a 6
  //   4*10 9*0 1 a 6 4*10 9*0 1 a 6 4*10 9*0 1 a 6 1 a 7 a 6 0 10 6*0 1 a 6 1 a 7 a 6 0 10 6*0 1 a 6 1 a 7
  //   a 6 0 10 6*0 1 a 6 13*0 1 a 6 4*10 9*0 1 a 6 4*10 9*0 1 a 6 13*0 1 a 6 13*0 1 a 6 13*0 1 a 6 13*0 1
  //   a 6 13*0 1 a 6 13*0 1 a 6 13*0 1 a 6 13*0 1 a 6 13*0 1 a 6 13*0 1 a 6 13*0 1 a 6 13*0 1 a 6 13*0 1 a
  //   6 13*0 1 a 6 13*0 1 a 6 13*0 1 a 6 13*0 1 a 6 13*0 1 a 6 13*0 1 a 6 13*0 1 a 6 13*0 1 a 6 13*0 1 a 6
  //   13*0 1 a 6 13*0 1 a 6 13*0 1 a 6 13*0 1 a 6 13*0 1 a 6 13*0 1 a 6 13*0 1 a 6 13*0 1 a 6 13*0 1 a 6
  //   13*0 1 a 6 13*0 1 a 6 13*0 1 a 6 13*0 1 a 6 13*0 1 a 6 13*0 1 a 6 13*0 1 a 6 13*0 1 a 6 13*0 1 a 6
  //   13*0 1 a 6 13*0 1 a 6 13*0 1 a 6 13*0 1 a 6 13*0 1 a 6 13*0 1 a 6 13*0 1 a 6 13*0 1 a 6 13*0 1 a 6
  //   13*0 1 a 6 13*0 1 a 6 13*0 1 a 6 13*0 1 a 6 13*0 1 a 6 13*0 1 a 6 13*0 1 a 6 13*0 1 a 6 13*0 1 a 6
  //   13*0 1 a 6 13*0 1 a 6 13*0 1 a 6 13*0 1 a 6 13*0 1 a 6 13*0 1 a 6 0 0 10 10*0 1 a 6 10 10 10 10*0 1
  //   a 6 1 2 e 10 9*0 1 a 6 0 1 a 6 10 8*0 1 a 6 0 0 0 10 9*0 1 a 6 4*10 9*0 1 a 6 0 0 0 10 9*0 1 a 6 0 0
  //   10 10*0 1 a 6 40 12*0 1 a 6 4*10 9*0 1 a 6 0 0 0 10 9*0 1 a 6 0 0 0 10 9*0 1 a 6 0 0 0 10 9*0 1 a 6
  //   13*0 1 a 6 2 1 e 0 10 8*0 1 a 6 0 10 10 10*0 1 a 6 1 a 6 10 9*0 1 a 6 1 2 e 10 9*0 1 a 6 5*10 8*0 1
  //   a 6 5*10 8*0 1 a 6 1 a 6 0 10 8*0 1 a 6 4*10 9*0 1 a 6 4*10 9*0 1 a 6 5*10 8*0 1 a 6 4*10 9*0 1 a 6
  //   4*10 9*0 1 a 6 1 a 6 0 10 8*0 1 a 6 1 a 6 0 10 8*0 1 a 6 1 a 6 0 10 8*0 1 a 6 13*0 1 a 6 4*10 9*0 1
  //   a 6 4*10 9*0 1 a 6 1 a 6 10 9*0 1 a 6 10 10 10 10*0 1 a 6 1 a 1 e 10 8*0 1 a 6 5*10 8*0 1 a 6 1 a 6
  //   0 10 8*0 1 a 6 4*10 9*0 1 a 6 1 a 6 0 0 10 7*0 1 a 6 1 a 6 0 10 8*0 1 a 6 1 a 46 0 10 8*0 1 a 6 4*10
  //   9*0 1 a 6 1 a 6 0 10 8*0 1 a 6 1 a 6 0 10 8*0 1 a 6 1 a 6 0 10 8*0 1 a 6 13*0 1 a 6 1 a 6 2 0 1 e 10
  //   5*0 1 a 6 1 a 10 10 9*0 1 a 6 1 a 7 a 6 10 7*0 1 a 6 10 10 10 10*0 1 a 6 5*10 8*0 1 a 6 0 1 a 6 10
  //   8*0 1 a 6 5*10 8*0 1 a 6 4*10 9*0 1 a 6 6*10 7*0 1 a 6 4*10 9*0 1 a 6 4*10 9*0 1 a 6 4*10 9*0 1 a 6
  //   1 a 7 a 6 0 10 6*0 1 a 6 1 a 7 a 6 0 10 6*0 1 a 6 1 a 7 a 6 0 10 6*0 1 a 6 13*0 1 a 6 4*10 9*0 1 a 6
  //   4*10 9*0 1 a 6 13*0 1 a 6 13*0 1 a 6 13*0 1 a 6 13*0 1 a 6 13*0 1 a 6 13*0 1 a 6 13*0 1 a 6 13*0 1 a
  //   6 13*0 1 a 6 13*0 1 a 6 13*0 1 a 6 13*0 1 a 6 13*0 1 a 6 13*0 1 a 6 13*0 1 a 6 13*0 1 a 6 13*0 1 a 6
  //   13*0 1 a 6 13*0 1 a 6 13*0 1 a 6 13*0 1 a 6 13*0 1 a 6 13*0 1 a 6 13*0 1 a 6 13*0 1 a 6 13*0 1 a 6
  //   13*0 1 a 6 13*0 1 a 6 13*0 1 a 6 13*0 1 a 6 13*0 1 a 6 13*0 1 a 6 13*0 1 a 6 13*0 1 a 6 13*0 1 a 6
  //   13*0 1 a 6 13*0 1 a 6 13*0 1 a 6 13*0 1 a 6 13*0 1 a 6 13*0 1 a 6 13*0 1 a 6 13*0 1 a 6 13*0 1 a 6
  //   13*0 1 a 6 13*0 1 a 6 13*0 1 a 6 13*0 1 a 6 13*0 1 a 6 13*0 1 a 6 13*0 1 a 6 13*0 1 a 6 13*0 1 a 6
  //   13*0 1 a 6 13*0 1 a 6 13*0 1 a 6 13*0 1 a 6 13*0 1 a 6 13*0 1 a 6 13*0 1 a 6 13*0 1 a 6 13*0 1 a 6
  //   13*0 1 a 6 13*0 1 a 6 0 0 10 10*0 1 a 6 10 10 10 10*0 1 a 6 1 2 e 10 9*0 1 a 6 0 1 a 6 10 8*0 1 a 6
  //   0 0 0 10 9*0 1 a 6 4*10 9*0 1 a 6 0 0 0 10 9*0 1 a 6 0 0 10 10*0 1 a 6 40 0 0 a0 9*0 1 a 6 4*10 9*0
  //   1 a 6 0 0 0 10 9*0 1 a 6 0 0 0 10 9*0 1 a 6 0 0 0 10 9*0 1 a 6 13*0 1 a 6 2 1 e 0 10 8*0 1 a 6 0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
  //   contents of EEPROM2 (hex, n*v repeats v):
  //   0 0 0 2a 4 30*0 62 0 4 13*0 5a 4 14*0 1 2 4 29*0 1 12 4 13*0 1 12 15*0 2a 0 46 4 27*0 1 32 4 13*0 1
  //   3a 4 13*0 1 22 4 30*0 62 4 13*0 80 80*0 1 2 4 93*0 1 32 4 13*0 1 3a 4 13*0 1 22 4 94*0 62 4 29*0 1 2
  //   4 31*0 12 4 14*0 12 13*0 2a 0 46 29*0 1 32 4 13*0 1 3a 4 13*0 1 22 4 30*0 2a 0 4 62 4 10*0 80 62*0
  //   5a 4 111*0 1 0 0 32 4 11*0 1 0 0 3a 4 11*0 1 0 0 22 4 1082*0 2a 4 30*0 62 0 4 13*0 5a 4 14*0 1 2 4
  //   29*0 1 12 4 13*0 1 12 15*0 2a 0 4 4 27*0 1 32 4 13*0 1 3a 4 13*0 1 22 4 30*0 62 4 13*0 80 80*0 1 2 4
  //   93*0 1 32 4 13*0 1 3a 4 13*0 1 22 4 94*0 62 4 29*0 1 2 4 31*0 12 4 14*0 12 13*0 2a 0 4 29*0 1 32 4
  //   13*0 1 3a 4 13*0 1 22 4 30*0 2a 0 4 62 4 10*0 80 62*0 5a 4 111*0 1 0 0 32 4 11*0 1 0 0 3a 4 11*0 1 0
  //   0 22 4 1082*0 2a 4 30*0 62 0 4 13*0 5a 4 14*0 1 2 4 29*0 1 12 4 13*0 1 12 15*0 2a 0 46 4 27*0 1 32 4
  //   13*0 1 3a 4 13*0 1 22 4 30*0 62 4 13*0 80 80*0 1 2 4 93*0 1 32 4 13*0 1 3a 4 13*0 1 22 4 94*0 62 4
  //   29*0 1 2 4 31*0 12 4 14*0 12 13*0 2a 0 46 29*0 1 32 4 13*0 1 3a 4 13*0 1 22 4 30*0 2a 0 4 62 4 10*0
  //   80 62*0 5a 4 111*0 1 0 0 32 4 11*0 1 0 0 3a 4 11*0 1 0 0 22 4 1082*0 2a 4 30*0 62 0 4 13*0 5a 4 14*0
  //   1 2 4 29*0 1 12 4 13*0 1 12 15*0 2a 0 4 4 27*0 1 32 4 13*0 1 3a 4 13*0 1 22 4 30*0 62 4 13*0 80 80*0
  //   1 2 4 93*0 1 32 4 13*0 1 3a 4 13*0 1 22 4 94*0 62 4 29*0 1 2 4 31*0 12 4 14*0 12 13*0 2a 0 4 29*0 1
  //   32 4 13*0 1 3a 4 13*0 1 22 4 30*0 2a 0 4 62 4 10*0 80 62*0 5a 4 111*0 1 0 0 32 4 11*0 1 0 0 3a 4
  //   11*0 1 0 0 22 4
  //   PCin
  //   PCout
  //   PCinc
  //   RFin
  //   RFout
  //   IRin
  //   Vout
  //   DSTsel
  //   TCend
  //   GOTO6
  //   SCld
  //   SCdec
  //   Xin
  //   Yin
  //   Yout
  //   ALU
  //   CONin
  //   MARin
  //   MDRen 
  //   WRsel 
  //   MEMsel 
endmodule

module instruction_register (
  input  CLK,
  input  RST,
  input  V_out,
  input  [15:0] D_BUS,
  input  IR_WR_EN,
  output [15:0] D_BUS_OUT,
  output [3:0] REG_SEL_DST,
  output [2:0] ADDR_MODE,
  output [3:0] REG_SEL_SRC,
  output [3:0] OP_CODE
);

  wire [7:7] IR_q;

  Register #(.width(16)) IR (
    .D(D_BUS), .en(IR_WR_EN), .clk(CLK), .Q({OP_CODE, REG_SEL_SRC, IR_q[7], ADDR_MODE, REG_SEL_DST}),
    .clr(RST));
  assign D_BUS_OUT = V_out ? {{12{1'b0}}, REG_SEL_DST} : 16'bz;  // Controlled_Buffer controlled_buffer_1

  // Other names for the same wires on the sheet: IR_L_O = V_out
endmodule

module memory_registers (
  input  CLK,
  input  RST,
  input  [15:0] D_BUS,
  input  MAR_WR_EN,
  input  [15:0] MEM_DATA_IN,
  input  MDR_EN,
  input  WR_SEL,
  input  MEM_SEL,
  output [15:0] MEM_ADDRESS_OUT,
  output [15:0] D_BUS_OUT,
  output [15:0] MEM_DATA_OUT,
  output RAM_WR_EN,
  output RAM_OUT_EN,
  output ROM_OUT_EN
);

  wire or_1_out, READ_FROM_BUS, READ_FROM_MEM, WRITE_TO_BUS, WRITE_TO_MEM;
  wire [15:0] controlled_buffer_1_out, MDR_q;

  assign controlled_buffer_1_out = READ_FROM_BUS ? D_BUS : 16'bz;  // Controlled_Buffer controlled_buffer_1
  Register #(.width(16)) MAR (.D(D_BUS), .en(MAR_WR_EN), .clk(CLK), .Q(MEM_ADDRESS_OUT), .clr(RST));
  assign controlled_buffer_1_out = READ_FROM_MEM ? MEM_DATA_IN : 16'bz;  // Controlled_Buffer controlled_buffer_2
  or or_1 (or_1_out, READ_FROM_BUS, READ_FROM_MEM);
  Register #(.width(16)) MDR (.D(controlled_buffer_1_out), .en(or_1_out), .clk(CLK), .Q(MDR_q), .clr(RST));
  Decoder #(.select(2)) decoder_1 (
    .out0(READ_FROM_BUS), .out1(WRITE_TO_BUS), .out2(READ_FROM_MEM), .out3(WRITE_TO_MEM),
    .sel({MEM_SEL, WR_SEL}), .en(MDR_EN));
  not not_1 (ROM_OUT_EN, MEM_ADDRESS_OUT[15]);
  and and_1 (RAM_OUT_EN, MEM_ADDRESS_OUT[15], READ_FROM_MEM);
  and and_2 (RAM_WR_EN, MEM_ADDRESS_OUT[15], WRITE_TO_MEM);
  assign D_BUS_OUT = WRITE_TO_BUS ? MDR_q : 16'bz;  // Controlled_Buffer controlled_buffer_3
  assign MEM_DATA_OUT = WRITE_TO_MEM ? MDR_q : 16'bz;  // Controlled_Buffer controlled_buffer_4
endmodule

module program_counter (
  input  CLK,
  input  RST,
  input  PC_OUT,
  input  PC_IN,
  input  PC_INC,
  input  [15:0] D_BUS,
  output [15:0] D_BUS_OUT
);

  wire [15:0] counter_1_q;

  Counter #(.max('hffff), .width(16)) counter_1 (
    .clr(RST), .load(PC_IN), .up(1'b1), .count(PC_INC), .clk(CLK), .D(D_BUS), .Q(counter_1_q));  // open: carry
  assign D_BUS_OUT = PC_OUT ? counter_1_q : 16'bz;  // Controlled_Buffer controlled_buffer_1
endmodule

module register_file (
  input  CLK,
  input  RST,
  input  [3:0] FLAGS_IN,
  input  RF_FL_IN,
  input  [15:0] DATA_IN,
  input  RF_IN,
  input  [3:0] REG_SEL_SRC,
  input  [3:0] REG_SEL_DST,
  input  [15:0] IN_REG,
  input  DST_SEL,
  input  REG_RD,
  output [15:0] DATA_OUT,
  output [3:0] FLAGS_OUT,
  output HLT,
  output [15:0] OUT_REG
);

  wire decoder_1_out1, decoder_1_out2, not_1_out, RD_EN_REG2, RD_EN_REG3, RD_EN_REG4, RD_EN_REG5, RD_EN_REG6,
       RD_EN_REG7, RD_EN_REG8, RD_EN_SP, RD_EN_SR, WR_EN_C, WR_EN_D, WR_EN_E, WR_EN_F, WR_EN_REG3,
       WR_EN_REG8, WR_EN_SP, WR_EN_SR;
  wire [3:0] multiplexer_1_out;
  wire [15:0] controlled_buffer_4_out, IN_REG2_q, multiplexer_2_out, REG4_q, REG5_q, REG6_q, REG7_q, REG8_q,
       SP_REG_REG0_q;
  wire [15:5] SR_REG_1_q;

  Hex_Digit_Display hex_digit_display_1 (.value(REG_SEL_DST));  // open: dp
  Hex_Digit_Display hex_digit_display_2 (.value(REG_SEL_SRC));  // open: dp
  LED led_1 (.in(not_1_out));
  not not_1 (not_1_out, DST_SEL);
  LED led_2 (.in(DST_SEL));
  Multiplexer #(.width(4)) multiplexer_1 (.in0(REG_SEL_SRC), .in1(REG_SEL_DST), .out(multiplexer_1_out), .sel(DST_SEL));
  // Probe on multiplexer_1_out
  Decoder #(.select(4)) decoder_1 (
    .out0(WR_EN_SP), .out1(decoder_1_out1), .out2(decoder_1_out2), .out3(WR_EN_REG3), .out4(WR_EN_C),
    .out5(WR_EN_D), .out6(WR_EN_E), .out7(WR_EN_F), .out8(WR_EN_REG8), .sel(multiplexer_1_out), .en(RF_IN));  // open: out9, out10, out11, out12, out13, out14, out15
  Decoder #(.select(4)) decoder_2 (
    .out0(RD_EN_SP), .out1(RD_EN_SR), .out2(RD_EN_REG2), .out3(RD_EN_REG3), .out4(RD_EN_REG4),
    .out5(RD_EN_REG5), .out6(RD_EN_REG6), .out7(RD_EN_REG7), .out8(RD_EN_REG8), .sel(multiplexer_1_out),
    .en(REG_RD));  // open: out9, out10, out11, out12, out13, out14, out15
  or or_1 (WR_EN_SR, RF_FL_IN, decoder_1_out1);
  Multiplexer #(.width(16)) multiplexer_2 (
    .in0(DATA_IN), .in1({{12{1'b0}}, FLAGS_IN}), .out(multiplexer_2_out), .sel(RF_FL_IN));
  Register #(.width(16)) SP_REG_REG0 (.D(DATA_IN), .en(WR_EN_SP), .clk(CLK), .Q(SP_REG_REG0_q), .clr(RST));
  Register #(.width(16)) SR_REG_1 (
    .D(multiplexer_2_out), .en(WR_EN_SR), .clk(CLK), .Q({SR_REG_1_q, HLT, FLAGS_OUT}), .clr(RST));
  Register #(.width(16)) IN_REG2 (.D(IN_REG), .en(1'b1), .clk(CLK), .Q(IN_REG2_q), .clr(RST));
  Register #(.width(16)) OUT_REG3 (.D(DATA_IN), .en(WR_EN_REG3), .clk(CLK), .Q(OUT_REG), .clr(RST));
  Register #(.width(16)) REG4 (.D(DATA_IN), .en(WR_EN_C), .clk(CLK), .Q(REG4_q), .clr(RST));
  Register #(.width(16)) REG5 (.D(DATA_IN), .en(WR_EN_D), .clk(CLK), .Q(REG5_q), .clr(RST));
  Register #(.width(16)) REG6 (.D(DATA_IN), .en(WR_EN_E), .clk(CLK), .Q(REG6_q), .clr(RST));
  Register #(.width(16)) REG7 (.D(DATA_IN), .en(WR_EN_F), .clk(CLK), .Q(REG7_q), .clr(RST));
  Register #(.width(16)) REG8 (.D(DATA_IN), .en(WR_EN_REG8), .clk(CLK), .Q(REG8_q), .clr(RST));
  assign DATA_OUT = RD_EN_SP ? SP_REG_REG0_q : 16'bz;  // Controlled_Buffer controlled_buffer_1
  assign DATA_OUT = RD_EN_SR ? {SR_REG_1_q, HLT, FLAGS_OUT} : 16'bz;  // Controlled_Buffer controlled_buffer_2
  assign DATA_OUT = RD_EN_REG2 ? IN_REG2_q : 16'bz;  // Controlled_Buffer controlled_buffer_3
  assign controlled_buffer_4_out = RD_EN_REG3 ? OUT_REG : 16'bz;  // Controlled_Buffer controlled_buffer_4
  assign DATA_OUT = RD_EN_REG4 ? REG4_q : 16'bz;  // Controlled_Buffer controlled_buffer_5
  assign DATA_OUT = RD_EN_REG5 ? REG5_q : 16'bz;  // Controlled_Buffer controlled_buffer_6
  assign DATA_OUT = RD_EN_REG6 ? REG6_q : 16'bz;  // Controlled_Buffer controlled_buffer_7
  assign DATA_OUT = RD_EN_REG7 ? REG7_q : 16'bz;  // Controlled_Buffer controlled_buffer_8
  assign DATA_OUT = RD_EN_REG8 ? REG8_q : 16'bz;  // Controlled_Buffer controlled_buffer_9

  // Other names for the same wires on the sheet: SR_D_IN[3:0] = FLAGS_IN
endmodule

module shift_control (
  input  CLK,
  input  RST,
  input  SHC_IN,
  input  SHC_DEC,
  input  [15:0] D_IN,
  output SHC_EQ0
);

  wire [3:0] counter_1_q;

  // Probe on D_IN[3:0]
  Counter #(.max('hf), .width(4)) counter_1 (
    .clr(RST), .load(SHC_IN), .up(1'b0), .count(SHC_DEC), .clk(CLK), .D(D_IN[3:0]), .Q(counter_1_q));  // open: carry
  nor nor_1 (SHC_EQ0, counter_1_q[3], counter_1_q[2], counter_1_q[1], counter_1_q[0]);
endmodule

module timing_control (
  input  RST,
  input  GOTO6,
  input  CLK,
  input  TC_END,
  output [3:0] T_OUT
);

  wire not_1_out, not_2_out, or_1_out;
  wire [3:0] controlled_buffer_1_out;

  or or_1 (or_1_out, GOTO6, TC_END);
  not not_1 (not_1_out, CLK);
  assign controlled_buffer_1_out = TC_END ? 4'b0000 : 4'bz;  // Controlled_Buffer controlled_buffer_1
  not not_2 (not_2_out, TC_END);
  Counter #(.max('hf), .width(4)) counter_1 (
    .clr(RST), .load(or_1_out), .up(1'b1), .count(1'b1), .clk(not_1_out), .D(controlled_buffer_1_out),
    .Q(T_OUT));  // open: carry
  assign controlled_buffer_1_out = not_2_out ? 4'b0110 : 4'bz;  // Controlled_Buffer controlled_buffer_2
endmodule

module z74_alu (
  input  RST,
  input  CLK,
  input  Y_OUT,
  input  Y_IN,
  input  X_in,
  input  [3:0] S_in,
  input  M_in,
  input  ALU_Carry_En,
  input  SH_EN,
  input  CYC_EN,
  input  [3:0] Flags_in,
  input  [15:0] DATAIN,
  output [15:0] Y_DATA_OUT,
  output [3:0] A_EQ_B,
  output [3:0] FLAGS_OUT
);

  wire A0, A1, A2, A3, A4, A5, A6, A7, A8, A9, A10, A11, A12, A13, A14, A15, and_1_out, and_2_out, and_3_out,
       and_4_out, and_5_out, and_6_out, and_7_out, and_8_out, B0, B1, B2, B3, B4, B5, B6, B7, B8, B9, B10,
       B11, B12, B13, B14, B15, C_in, F0, F1, F2, F3, F4, F5, F6, F7, F8, F9, F10, F11, F12, F13, F14,
       n74181_2_p11, n74181_3_p11, n74181_4_p11, n74181_4_p25, nor_1_out, nor_2_out, nor_3_out, nor_4_out,
       nor_5_out, nor_6_out, nor_7_out, nor_8_out, not_4_out, not_5_out, not_7_out, X_GB, Y_GB, Y_MN, Y_O_1,
       Y_O_2, Y_O_3, Y_O_4, Y_O_5, Y_O_6, Y_O_7, Y_O_8, Y_O_9, Y_O_10, Y_O_11, Y_O_12, Y_O_13, Y_O_14,
       Y_O_15, Y_O_16;

  not not_1 (Y_MN, Y_OUT);
  not not_2 (Y_GB, Y_IN);
  not not_3 (X_GB, X_in);
  extra_shifter extra_shifter_1 (
    .CYC_EN(CYC_EN), .D_IN(DATAIN), .SH_EN(SH_EN),
    .out_4({A15, A14, A13, A12, A11, A10, A9, A8, A7, A6, A5, A4, A3, A2, A1, A0}));
  not not_4 (not_4_out, ALU_Carry_En);
  not not_5 (not_5_out, Flags_in[0]);
  and and_1 (and_1_out, S_in[0], not_4_out);
  and and_2 (and_2_out, S_in[0], not_5_out);
  or or_1 (C_in, and_1_out, and_2_out);
  Hex_Digit_Display hex_digit_display_1 (.value({A15, A14, A13, A12}));  // open: dp
  ttl74173 X0 (
    .D1(DATAIN[0]), .D2(DATAIN[1]), .D3(DATAIN[2]), .D4(DATAIN[3]), .CLK(CLK), .RST(RST), .G1(X_GB),
    .G2(X_GB), .M(1'b0), .N(1'b0), .Q1(B0), .Q2(B1), .Q3(B2), .Q4(B3));
  ttl74173 X1 (
    .D1(DATAIN[4]), .D2(DATAIN[5]), .D3(DATAIN[6]), .D4(DATAIN[7]), .CLK(CLK), .RST(RST), .G1(X_GB),
    .G2(X_GB), .M(1'b0), .N(1'b0), .Q1(B4), .Q2(B5), .Q3(B6), .Q4(B7));
  ttl74173 X2 (
    .D1(DATAIN[8]), .D2(DATAIN[9]), .D3(DATAIN[10]), .D4(DATAIN[11]), .CLK(CLK), .RST(RST), .G1(X_GB),
    .G2(X_GB), .M(1'b0), .N(1'b0), .Q1(B8), .Q2(B9), .Q3(B10), .Q4(B11));
  ttl74173 X3 (
    .D1(DATAIN[12]), .D2(DATAIN[13]), .D3(DATAIN[14]), .D4(DATAIN[15]), .CLK(CLK), .RST(RST), .G1(X_GB),
    .G2(X_GB), .M(1'b0), .N(1'b0), .Q1(B12), .Q2(B13), .Q3(B14), .Q4(B15));
  Hex_Digit_Display #(.decimalPoint("false")) hex_digit_display_2 (.value({A11, A10, A9, A8}));
  Hex_Digit_Display hex_digit_display_3 (.value({A7, A6, A5, A4}));  // open: dp
  Hex_Digit_Display hex_digit_display_4 (.value({A3, A2, A1, A0}));  // open: dp
  Hex_Digit_Display hex_digit_display_5 (.value({FLAGS_OUT[2], F14, F13, F12}));  // open: dp
  Hex_Digit_Display #(.decimalPoint("false")) hex_digit_display_6 (.value({F11, F10, F9, F8}));
  Hex_Digit_Display hex_digit_display_7 (.value({F7, F6, F5, F4}));  // open: dp
  Hex_Digit_Display hex_digit_display_8 (.value({F3, F2, F1, F0}));  // open: dp
  // _74181 #(.ShowInternalStructure("true")) 74181_1: pin names not known; wires that end beside it: B0, A0, S_in[3], S_in[2], S_in[1], S_in[0], C_in, A1, B1, A2, B2, A3, B3
  // _74181 #(.ShowInternalStructure("true")) 74181_2: pin names not known; wires that end beside it: M_in, F0, F1, F2, B4, A4, S_in[3], S_in[2], S_in[1], S_in[0], n74181_2_p11, n74181_2_p11, A_EQ_B[3], F3, A5, B5, A6, B6, A7, B7
  // _74181 #(.ShowInternalStructure("true")) 74181_3: pin names not known; wires that end beside it: M_in, F4, F5, F6, B8, A8, S_in[3], S_in[2], S_in[1], S_in[0], n74181_3_p11, n74181_3_p11, A_EQ_B[2], F7, A9, B9, A10, B10, A11, B11
  // _74181 #(.ShowInternalStructure("true")) 74181_4: pin names not known; wires that end beside it: M_in, F8, F9, F10, B12, A12, S_in[3], S_in[2], S_in[1], S_in[0], n74181_4_p11, M_in, F12, F13, F14, n74181_4_p11, A_EQ_B[1], F11, A13, B13, A14, B14, A15, B15, n74181_4_p25, A_EQ_B[0], FLAGS_OUT[2]
  not not_6 (FLAGS_OUT[0], n74181_4_p25);
  Hex_Digit_Display hex_digit_display_9 (.value({Y_O_16, Y_O_15, Y_O_14, Y_O_13}));  // open: dp
  Hex_Digit_Display #(.decimalPoint("false")) hex_digit_display_10 (.value({Y_O_12, Y_O_11, Y_O_10, Y_O_9}));
  Hex_Digit_Display hex_digit_display_11 (.value({Y_O_8, Y_O_7, Y_O_6, Y_O_5}));  // open: dp
  nor nor_1 (nor_1_out, F0, F1);
  nor nor_2 (nor_2_out, F2, F3);
  nor nor_3 (nor_3_out, F4, F5);
  nor nor_4 (nor_4_out, F6, F7);
  nor nor_5 (nor_5_out, F8, F9);
  nor nor_6 (nor_6_out, F10, F11);
  nor nor_7 (nor_7_out, F12, F13);
  nor nor_8 (nor_8_out, F14, FLAGS_OUT[2]);
  Hex_Digit_Display hex_digit_display_12 (.value({Y_O_4, Y_O_3, Y_O_2, Y_O_1}));  // open: dp
  and and_3 (and_3_out, nor_1_out, nor_2_out);
  and and_4 (and_4_out, nor_3_out, nor_4_out);
  and and_5 (and_5_out, nor_5_out, nor_6_out);
  and and_6 (and_6_out, nor_7_out, nor_8_out);
  not not_7 (not_7_out, Y_MN);
  assign Y_DATA_OUT = not_7_out ? {Y_O_16, Y_O_15, Y_O_14, Y_O_13, Y_O_12, Y_O_11, Y_O_10, Y_O_9, Y_O_8, Y_O_7, Y_O_6, Y_O_5, Y_O_4, Y_O_3, Y_O_2, Y_O_1} : 16'bz;  // Controlled_Buffer controlled_buffer_1
  and and_7 (and_7_out, and_3_out, and_4_out);
  and and_8 (and_8_out, and_5_out, and_6_out);
  and and_9 (FLAGS_OUT[1], and_7_out, and_8_out);
  not not_8 (FLAGS_OUT[3], F0);
  ttl74173 ttl74173_1 (
    .D1(F0), .D2(F1), .D3(F2), .D4(F3), .CLK(CLK), .RST(RST), .G1(Y_GB), .G2(Y_GB), .M(1'b0), .N(1'b0),
    .Q1(Y_O_1), .Q2(Y_O_2), .Q3(Y_O_3), .Q4(Y_O_4));
  ttl74173 ttl74173_2 (
    .D1(F4), .D2(F5), .D3(F6), .D4(F7), .CLK(CLK), .RST(RST), .G1(Y_GB), .G2(Y_GB), .M(1'b0), .N(1'b0),
    .Q1(Y_O_5), .Q2(Y_O_6), .Q3(Y_O_7), .Q4(Y_O_8));
  ttl74173 ttl74173_3 (
    .D1(F8), .D2(F9), .D3(F10), .D4(F11), .CLK(CLK), .RST(RST), .G1(Y_GB), .G2(Y_GB), .M(1'b0), .N(1'b0),
    .Q1(Y_O_9), .Q2(Y_O_10), .Q3(Y_O_11), .Q4(Y_O_12));
  ttl74173 ttl74173_4 (
    .D1(F12), .D2(F13), .D3(F14), .D4(FLAGS_OUT[2]), .CLK(CLK), .RST(RST), .G1(Y_GB), .G2(Y_GB), .M(1'b0),
    .N(1'b0), .Q1(Y_O_13), .Q2(Y_O_14), .Q3(Y_O_15), .Q4(Y_O_16));

  // Other names for the same wires on the sheet: A_EQ_B_4 = A_EQ_B[0]; A_EQ_B_3 = A_EQ_B[1]; A_EQ_B_2 = A_EQ_B[2];
  //   A_EQ_B_1 = A_EQ_B[3]; ALU_OUT[15:0] = Y_DATA_OUT; D_IN[15:0] = DATAIN; X0 = DATAIN[0]; X1 = DATAIN[1];
  //   X2 = DATAIN[2]; X3 = DATAIN[3]; X4 = DATAIN[4]; X5 = DATAIN[5]; X6 = DATAIN[6]; X7 = DATAIN[7]; X8 = DATAIN[8];
  //   X9 = DATAIN[9]; X10 = DATAIN[10]; X11 = DATAIN[11]; X12 = DATAIN[12]; X13 = DATAIN[13]; X14 = DATAIN[14];
  //   X15 = DATAIN[15]; Flags_Carry = Flags_in[0]; C_F_OUT = FLAGS_OUT[0]; Z_F_OUT = FLAGS_OUT[1]; F15 = FLAGS_OUT[2];
  //   N_F_OUT = FLAGS_OUT[2]; E_F_OUT = FLAGS_OUT[3]; S0 = S_in[0]

  // Notes on the sheet:
  //   its possible to replace the or  gate
  //   X
  //   RES
  //   Y
endmodule

module test_z74_alu (
  input  RST,
  input  CLK,
  input  [3:0] S_in,
  input  M_in,
  input  ALU_Carry_En,
  input  [3:0] Flags_in,
  input  [15:0] A_IN,
  input  [15:0] B_IN,
  output [3:0] A_EQ_B,
  output C_out,
  output [15:0] RESULT
);

  wire and_1_out, and_2_out, C_in, C_out_t, n74181_2_p11, n74181_3_p11, n74181_4_p11, not_2_out, not_3_out;

  not not_1 (C_out, C_out_t);
  not not_2 (not_2_out, ALU_Carry_En);
  not not_3 (not_3_out, Flags_in[0]);
  and and_1 (and_1_out, S_in[0], not_2_out);
  and and_2 (and_2_out, S_in[0], not_3_out);
  or or_1 (C_in, and_1_out, and_2_out);
  // _74181 #(.ShowInternalStructure("true")) 74181_1: pin names not known; wires that end beside it: B_IN[0], A_IN[0], S_in[3], S_in[2], S_in[1], S_in[0], C_in, A_IN[1], B_IN[1], A_IN[2], B_IN[2], A_IN[3], B_IN[3]
  // _74181 #(.ShowInternalStructure("true")) 74181_2: pin names not known; wires that end beside it: M_in, RESULT[0], RESULT[1], RESULT[2], B_IN[4], A_IN[4], S_in[3], S_in[2], S_in[1], S_in[0], n74181_2_p11, n74181_2_p11, A_EQ_B[3], RESULT[3], A_IN[5], B_IN[5], A_IN[6], B_IN[6], A_IN[7], B_IN[7]
  // _74181 #(.ShowInternalStructure("true")) 74181_3: pin names not known; wires that end beside it: M_in, RESULT[4], RESULT[5], RESULT[6], B_IN[8], A_IN[8], S_in[3], S_in[2], S_in[1], S_in[0], n74181_3_p11, n74181_3_p11, A_EQ_B[2], RESULT[7], A_IN[9], B_IN[9], A_IN[10], B_IN[10], A_IN[11], B_IN[11]
  // _74181 #(.ShowInternalStructure("true")) 74181_4: pin names not known; wires that end beside it: M_in, RESULT[8], RESULT[9], RESULT[10], B_IN[12], A_IN[12], S_in[3], S_in[2], S_in[1], S_in[0], n74181_4_p11, M_in, RESULT[12], RESULT[13], RESULT[14], n74181_4_p11, A_EQ_B[1], RESULT[11], A_IN[13], B_IN[13], A_IN[14], B_IN[14], A_IN[15], B_IN[15], C_out_t, A_EQ_B[0], RESULT[15]

  // Other names for the same wires on the sheet: A_EQ_B_4 = A_EQ_B[0]; A_EQ_B_3 = A_EQ_B[1]; A_EQ_B_2 = A_EQ_B[2];
  //   A_EQ_B_1 = A_EQ_B[3]; A0 = A_IN[0]; A1 = A_IN[1]; A2 = A_IN[2]; A3 = A_IN[3]; A4 = A_IN[4]; A5 = A_IN[5];
  //   A6 = A_IN[6]; A7 = A_IN[7]; A8 = A_IN[8]; A9 = A_IN[9]; A10 = A_IN[10]; A11 = A_IN[11]; A12 = A_IN[12];
  //   A13 = A_IN[13]; A14 = A_IN[14]; A15 = A_IN[15]; B0 = B_IN[0]; B1 = B_IN[1]; B2 = B_IN[2]; B3 = B_IN[3];
  //   B4 = B_IN[4]; B5 = B_IN[5]; B6 = B_IN[6]; B7 = B_IN[7]; B8 = B_IN[8]; B9 = B_IN[9]; B10 = B_IN[10];
  //   B11 = B_IN[11]; B12 = B_IN[12]; B13 = B_IN[13]; B14 = B_IN[14]; B15 = B_IN[15]; Flags_Carry = Flags_in[0];
  //   F0 = RESULT[0]; F1 = RESULT[1]; F2 = RESULT[2]; F3 = RESULT[3]; F4 = RESULT[4]; F5 = RESULT[5]; F6 = RESULT[6];
  //   F7 = RESULT[7]; F8 = RESULT[8]; F9 = RESULT[9]; F10 = RESULT[10]; F11 = RESULT[11]; F12 = RESULT[12];
  //   F13 = RESULT[13]; F14 = RESULT[14]; F15 = RESULT[15]; S0 = S_in[0]

  // Notes on the sheet:
  //   its possible to replace the or  gate
endmodule

module ttl74173 (
  input  M,
  input  N,
  input  G1,
  input  G2,
  input  CLK,
  input  RST,
  input  D1,
  input  D2,
  input  D3,
  input  D4,
  output Q1,
  output Q2,
  output Q3,
  output Q4
);

  wire and_3_out, and_4_out, and_5_out, and_6_out, and_7_out, and_8_out, and_9_out, and_10_out, d_ff_1_q,
       d_ff_1_qn, d_ff_2_q, d_ff_2_qn, d_ff_3_q, d_ff_3_qn, d_ff_4_q, d_ff_4_qn, G12_AND, G12_NOT, MN_AND,
       not_1_out, not_2_out, not_3_out, not_4_out, not_6_out, not_7_out, not_8_out, not_9_out, or_1_out,
       or_2_out, or_3_out, or_4_out;

  not not_1 (not_1_out, G1);
  not not_2 (not_2_out, G2);
  not not_3 (not_3_out, M);
  not not_4 (not_4_out, N);
  and and_1 (G12_AND, not_1_out, not_2_out);
  not not_5 (G12_NOT, G12_AND);
  and and_2 (MN_AND, not_3_out, not_4_out);
  and and_3 (and_3_out, d_ff_1_q, G12_NOT);
  or or_1 (or_1_out, and_3_out, and_4_out);
  and and_4 (and_4_out, G12_AND, D1);
  and and_5 (and_5_out, d_ff_2_q, G12_NOT);
  or or_2 (or_2_out, and_5_out, and_6_out);
  and and_6 (and_6_out, G12_AND, D2);
  and and_7 (and_7_out, d_ff_3_q, G12_NOT);
  or or_3 (or_3_out, and_7_out, and_8_out);
  and and_8 (and_8_out, G12_AND, D3);
  and and_9 (and_9_out, d_ff_4_q, G12_NOT);
  or or_4 (or_4_out, and_9_out, and_10_out);
  and and_10 (and_10_out, G12_AND, D4);
  D_Flip_Flop d_ff_1 (.D(or_1_out), .clk(CLK), .Q(d_ff_1_q), .Qn(d_ff_1_qn), .reset(RST));  // open: preset
  D_Flip_Flop d_ff_2 (.D(or_2_out), .clk(CLK), .Q(d_ff_2_q), .Qn(d_ff_2_qn), .reset(RST));  // open: preset
  D_Flip_Flop d_ff_3 (.D(or_3_out), .clk(CLK), .Q(d_ff_3_q), .Qn(d_ff_3_qn), .reset(RST));  // open: preset
  D_Flip_Flop d_ff_4 (.D(or_4_out), .clk(CLK), .Q(d_ff_4_q), .Qn(d_ff_4_qn), .reset(RST));  // open: preset
  not not_6 (not_6_out, d_ff_1_qn);
  not not_7 (not_7_out, d_ff_2_qn);
  not not_8 (not_8_out, d_ff_3_qn);
  not not_9 (not_9_out, d_ff_4_qn);
  assign Q1 = MN_AND ? not_6_out : 1'bz;  // Controlled_Buffer controlled_buffer_1
  assign Q2 = MN_AND ? not_7_out : 1'bz;  // Controlled_Buffer controlled_buffer_2
  assign Q3 = MN_AND ? not_8_out : 1'bz;  // Controlled_Buffer controlled_buffer_3
  assign Q4 = MN_AND ? not_9_out : 1'bz;  // Controlled_Buffer controlled_buffer_4
endmodule

module extra_alu_input (
  input  [3:0] Input,
  output [3:0] S,
  output M,
  output C_EN,
  output SH_EN,
  output CYC_EN
);

  wire and_1_out, and_2_out, and_3_out, and_4_out, and_5_out, and_6_out, and_7_out, and_8_out, and_9_out,
       and_10_out, and_11_out, and_13_out, and_14_out, and_15_out, and_16_out, and_17_out, and_18_out,
       and_19_out, and_20_out, and_21_out, and_22_out, and_23_out, and_24_out, and_25_out, and_26_out,
       not_1_out, not_2_out, not_3_out, not_4_out, or_1_out, or_2_out, or_3_out, or_5_out, or_6_out,
       or_8_out, or_9_out, or_10_out, or_11_out;

  not not_1 (not_1_out, Input[3]);
  not not_2 (not_2_out, Input[2]);
  not not_3 (not_3_out, Input[1]);
  not not_4 (not_4_out, Input[0]);
  and and_1 (and_1_out, not_2_out, not_3_out);
  and and_2 (and_2_out, Input[2], Input[1]);
  and and_3 (and_3_out, Input[3], not_4_out);
  and and_4 (and_4_out, not_3_out, Input[0]);
  and and_5 (and_5_out, not_1_out, not_2_out);
  and and_6 (and_6_out, Input[1], not_4_out);
  and and_7 (and_7_out, Input[1], not_4_out);
  and and_8 (and_8_out, Input[2], Input[1]);
  and and_9 (and_9_out, not_1_out, Input[1]);
  and and_10 (and_10_out, Input[3], not_2_out);
  and and_11 (and_11_out, Input[3], not_2_out);
  and and_12 (C_EN, not_1_out, Input[0]);
  and and_13 (and_13_out, Input[3], not_2_out);
  or or_1 (or_1_out, and_1_out, and_2_out);
  or or_2 (or_2_out, and_3_out, and_4_out);
  and and_14 (and_14_out, and_5_out, and_6_out);
  and and_15 (and_15_out, Input[2], not_3_out);
  and and_16 (and_16_out, Input[2], Input[0]);
  and and_17 (and_17_out, Input[3], not_3_out);
  or or_3 (or_3_out, and_7_out, Input[2]);
  and and_18 (and_18_out, Input[3], not_3_out);
  and and_19 (and_19_out, not_2_out, not_3_out);
  and and_20 (and_20_out, not_3_out, Input[0]);
  and and_21 (and_21_out, and_8_out, not_4_out);
  and and_22 (and_22_out, Input[3], not_3_out);
  and and_23 (and_23_out, and_9_out, Input[0]);
  and and_24 (and_24_out, not_1_out, Input[2]);
  and and_25 (and_25_out, and_10_out, not_3_out);
  and and_26 (and_26_out, and_11_out, not_4_out);
  and and_27 (SH_EN, and_13_out, not_3_out);
  or or_4 (S[3], or_1_out, or_2_out);
  or or_5 (or_5_out, and_14_out, and_15_out);
  or or_6 (or_6_out, and_16_out, and_17_out);
  or or_7 (S[1], or_3_out, and_18_out);
  or or_8 (or_8_out, and_19_out, and_20_out);
  or or_9 (or_9_out, and_21_out, and_22_out);
  or or_10 (or_10_out, and_23_out, and_24_out);
  or or_11 (or_11_out, and_25_out, and_26_out);
  or or_12 (S[2], or_5_out, or_6_out);
  or or_13 (S[0], or_8_out, or_9_out);
  or or_14 (M, or_10_out, or_11_out);

  assign CYC_EN = Input[0];
endmodule

module extra_shifter (
  input  CYC_EN,
  input  [15:0] D_IN,
  input  SH_EN,
  output [15:0] out_4
);

  wire [15:15] and_1_out;

  and and_1 (and_1_out[15], D_IN[0], CYC_EN);
  Multiplexer #(.width(16)) multiplexer_1 (.in0(D_IN), .in1({and_1_out[15], D_IN[15:1]}), .out(out_4), .sel(SH_EN));

  // Notes on the sheet:
  //   Maybe use some and gates instead of mux
endmodule

module control_logic_backup (
  input  CON,
  input  N_EQ_0,
  input  [2:0] ADDRESSING_MODE,
  input  [4:0] OPCODE,
  input  [3:0] T_TIME,
  output PCin,
  output PCout,
  output PCinc,
  output RFin,
  output RFout,
  output DSTsel,
  output IRin,
  output IRout,
  output MARin,
  output MDRen,
  output WRsel,
  output MEMsel,
  output TCend,
  output GOTO6,
  output HLT,
  output UNDEFINED_1_7,
  output Xin,
  output Yin,
  output Yout,
  output ALUctrl_0,
  output ALUctrl_1,
  output ALUctrl_2,
  output ALUctrl_3,
  output UNDEFINED_2_7,
  output RST_EN,
  output IN_REG,
  output OUT_REG,
  output CONin,
  output SCld,
  output SCdec,
  output UNDEFINED_3_6,
  output UNDEFINED_3_7
);

  ROM #(.addrWidth(15)) EEPROM0 (
    .addr({1'b0, CON, N_EQ_0, ADDRESSING_MODE, OPCODE, T_TIME}),
    .data({IRout, IRin, DSTsel, RFout, RFin, PCinc, PCout, PCin}));
  ROM #(.addrWidth(15)) EEPROM1 (
    .addr({1'b0, CON, N_EQ_0, ADDRESSING_MODE, OPCODE, T_TIME}),
    .data({UNDEFINED_1_7, HLT, GOTO6, TCend, MEMsel, WRsel, MDRen, MARin}));
  ROM #(.addrWidth(15)) EEPROM2 (
    .addr({1'b0, CON, N_EQ_0, ADDRESSING_MODE, OPCODE, T_TIME}),
    .data({UNDEFINED_2_7, ALUctrl_3, ALUctrl_2, ALUctrl_1, ALUctrl_0, Yout, Yin, Xin}));
  ROM #(.addrWidth(15)) EEPROM3 (
    .addr({1'b0, CON, N_EQ_0, ADDRESSING_MODE, OPCODE, T_TIME}),
    .data({UNDEFINED_3_7, UNDEFINED_3_6, SCdec, SCld, CONin, OUT_REG, IN_REG, RST_EN}));
endmodule

module ttl7400_instruction_register (
  input  CLK,
  input  RST,
  input  IR_OUT,
  input  IR_WR_EN,
  input  [15:0] D_BUS,
  output [15:0] D_BUS_OUT,
  output [3:0] REG_SEL_DST,
  output [3:0] REG_SEL_SRC,
  output [2:0] ADDR_MODE,
  output [4:0] OP_CODE
);

  _7404 #(.ShowInternalStructure("true")) u_7404_1 ();  // open: pin1, pin2, pin3, pin4, pin5, pin6, pin13, pin12, pin11, pin10, pin9, pin8
  ttl74173 IR_3 ();  // open: D1, D2, D3, D4, CLK, RST, G1, G2, M, N, Q1, Q2, Q3, Q4
  ttl74173 IR_2 ();  // open: D1, D2, D3, D4, CLK, RST, G1, G2, M, N, Q1, Q2, Q3, Q4
  ttl74173 IR_1 ();  // open: D1, D2, D3, D4, CLK, RST, G1, G2, M, N, Q1, Q2, Q3, Q4
  ttl74173 IR_0 ();  // open: D1, D2, D3, D4, CLK, RST, G1, G2, M, N, Q1, Q2, Q3, Q4
  Register #(.width(16)) IR (
    .en(IR_WR_EN), .clk(CLK), .Q({OP_CODE, ADDR_MODE, REG_SEL_SRC, REG_SEL_DST}), .clr(RST));  // open: D
  assign D_BUS_OUT = IR_OUT ? {OP_CODE, ADDR_MODE, REG_SEL_SRC, REG_SEL_DST} : 16'bz;  // Controlled_Buffer controlled_buffer_1

  // Other names for the same wires on the sheet: IR_L_O = IR_OUT
endmodule

module carry_test (
  input  [3:0] S,
  input  M,
  input  Cin,
  input  [7:0] A,
  input  [7:0] B,
  output [7:0] Fout,
  output Cout
);

  wire n74181_1_p13, n74181_2_p2, n74181_2_p21;

  // _74181 #(.ShowInternalStructure("true")) 74181_1: pin names not known; wires that end beside it: B[0], A[1], A[0], B[1], S[3], A[2], S[2], B[2], S[1], A[3], S[0], B[3], n74181_1_p13
  not not_1 (n74181_1_p13, Cin);
  // _74181 #(.ShowInternalStructure("true")) 74181_2: pin names not known; wires that end beside it: M, n74181_2_p2, Fout[0], Fout[1], Fout[2], Fout[3], B[4], A[5], A[4], B[5], S[3], A[6], S[2], B[6], S[1], A[7], S[0], B[7], n74181_2_p2, M, n74181_2_p21, Fout[4], Fout[5], Fout[6], Fout[7]
  not not_2 (Cout, n74181_2_p21);

  // Other names for the same wires on the sheet: F0 = Fout[0]; F1 = Fout[1]; F2 = Fout[2]; F3 = Fout[3]; F4 = Fout[4];
  //   F5 = Fout[5]; F6 = Fout[6]; F7 = Fout[7]
endmodule

module z74alu_backup (
  input  RST,
  input  CLK,
  input  Y_OUT,
  input  Y_IN,
  input  X_in,
  input  [3:0] S_in,
  input  M_in,
  input  ALU_Carry_En,
  input  SH_EN,
  input  CYC_EN,
  input  [3:0] Flags_in,
  input  [15:0] DATAIN,
  output [15:0] Y_DATA_OUT,
  output [3:0] A_EQ_B,
  output [3:0] FLAGS_OUT
);

  wire A0, A1, A2, A3, A4, A5, A6, A7, A8, A9, A10, A11, A12, A13, A14, A15, and_1_out, and_2_out, and_3_out,
       and_4_out, and_5_out, and_6_out, C_in, F0, F1, F2, F3, F4, F5, F6, F7, F8, F9, F10, F11, F12, F13,
       F14, n74181_2_p11, n74181_3_p11, n74181_4_p11, n74181_4_p25, nor_1_out, nor_2_out, nor_3_out,
       nor_4_out, nor_5_out, nor_6_out, nor_7_out, nor_8_out, not_4_out, not_6_out, X1, X2, X3, X4, X5, X6,
       X7, X8, X9, X10, X11, X12, X13, X14, X15, X16, X_GB, Y_GB, Y_MN, Y_O_1, Y_O_2, Y_O_3, Y_O_4, Y_O_5,
       Y_O_6, Y_O_7, Y_O_8, Y_O_9, Y_O_10, Y_O_11, Y_O_12, Y_O_13, Y_O_14, Y_O_15, Y_O_16;

  not not_1 (Y_MN, Y_OUT);
  not not_2 (Y_GB, Y_IN);
  not not_3 (X_GB, X_in);
  extra_shifter extra_shifter_1 (
    .CYC_EN(CYC_EN), .D_IN(DATAIN), .SH_EN(SH_EN),
    .out_4({X16, X15, X14, X13, X12, X11, X10, X9, X8, X7, X6, X5, X4, X3, X2, X1}));
  Hex_Digit_Display hex_digit_display_1 (.value({A15, A14, A13, A12}));  // open: dp
  ttl74173 X0 (
    .D1(X1), .D2(X2), .D3(X3), .D4(X4), .CLK(CLK), .RST(RST), .G1(X_GB), .G2(X_GB), .M(1'b0), .N(1'b0),
    .Q1(A0), .Q2(A1), .Q3(A2), .Q4(A3));
  ttl74173 u_X1 (
    .D1(X5), .D2(X6), .D3(X7), .D4(X8), .CLK(CLK), .RST(RST), .G1(X_GB), .G2(X_GB), .M(1'b0), .N(1'b0),
    .Q1(A4), .Q2(A5), .Q3(A6), .Q4(A7));
  ttl74173 u_X2 (
    .D1(X9), .D2(X10), .D3(X11), .D4(X12), .CLK(CLK), .RST(RST), .G1(X_GB), .G2(X_GB), .M(1'b0), .N(1'b0),
    .Q1(A8), .Q2(A9), .Q3(A10), .Q4(A11));
  ttl74173 u_X3 (
    .D1(X13), .D2(X14), .D3(X15), .D4(X16), .CLK(CLK), .RST(RST), .G1(X_GB), .G2(X_GB), .M(1'b0), .N(1'b0),
    .Q1(A12), .Q2(A13), .Q3(A14), .Q4(A15));
  Hex_Digit_Display #(.decimalPoint("false")) hex_digit_display_2 (.value({A11, A10, A9, A8}));
  Hex_Digit_Display hex_digit_display_3 (.value({A7, A6, A5, A4}));  // open: dp
  Hex_Digit_Display hex_digit_display_4 (.value({A3, A2, A1, A0}));  // open: dp
  Hex_Digit_Display hex_digit_display_5 (.value({FLAGS_OUT[2], F14, F13, F12}));  // open: dp
  Hex_Digit_Display #(.decimalPoint("false")) hex_digit_display_6 (.value({F11, F10, F9, F8}));
  not not_4 (not_4_out, C_in);
  Hex_Digit_Display hex_digit_display_7 (.value({F7, F6, F5, F4}));  // open: dp
  Hex_Digit_Display hex_digit_display_8 (.value({F3, F2, F1, F0}));  // open: dp
  // _74181 #(.ShowInternalStructure("true")) 74181_1: pin names not known; wires that end beside it: DATAIN[0], A0, S_in[3], S_in[2], S_in[1], S_in[0], not_4_out, A1, DATAIN[1], A2, DATAIN[2], A3, DATAIN[3]
  // _74181 #(.ShowInternalStructure("true")) 74181_2: pin names not known; wires that end beside it: M_in, F0, F1, F2, DATAIN[4], A4, S_in[3], S_in[2], S_in[1], S_in[0], n74181_2_p11, n74181_2_p11, A_EQ_B[3], F3, A5, DATAIN[5], A6, DATAIN[6], A7, DATAIN[7]
  // _74181 #(.ShowInternalStructure("true")) 74181_3: pin names not known; wires that end beside it: M_in, F4, F5, F6, DATAIN[8], A8, S_in[3], S_in[2], S_in[1], S_in[0], n74181_3_p11, n74181_3_p11, A_EQ_B[2], F7, A9, DATAIN[9], A10, DATAIN[10], A11, DATAIN[11]
  // _74181 #(.ShowInternalStructure("true")) 74181_4: pin names not known; wires that end beside it: M_in, F8, F9, F10, DATAIN[12], A12, S_in[3], S_in[2], S_in[1], S_in[0], n74181_4_p11, M_in, F12, F13, F14, n74181_4_p11, A_EQ_B[1], F11, A13, DATAIN[13], A14, DATAIN[14], A15, DATAIN[15], n74181_4_p25, A_EQ_B[0], FLAGS_OUT[2]
  not not_5 (FLAGS_OUT[0], n74181_4_p25);
  Hex_Digit_Display hex_digit_display_9 (.value({Y_O_16, Y_O_15, Y_O_14, Y_O_13}));  // open: dp
  Hex_Digit_Display #(.decimalPoint("false")) hex_digit_display_10 (.value({Y_O_12, Y_O_11, Y_O_10, Y_O_9}));
  Hex_Digit_Display hex_digit_display_11 (.value({Y_O_8, Y_O_7, Y_O_6, Y_O_5}));  // open: dp
  nor nor_1 (nor_1_out, F0, F1);
  nor nor_2 (nor_2_out, F2, F3);
  nor nor_3 (nor_3_out, F4, F5);
  nor nor_4 (nor_4_out, F6, F7);
  nor nor_5 (nor_5_out, F8, F9);
  nor nor_6 (nor_6_out, F10, F11);
  nor nor_7 (nor_7_out, F12, F13);
  nor nor_8 (nor_8_out, F14, FLAGS_OUT[2]);
  Hex_Digit_Display hex_digit_display_12 (.value({Y_O_4, Y_O_3, Y_O_2, Y_O_1}));  // open: dp
  and and_1 (and_1_out, nor_1_out, nor_2_out);
  and and_2 (and_2_out, nor_3_out, nor_4_out);
  and and_3 (and_3_out, nor_5_out, nor_6_out);
  and and_4 (and_4_out, nor_7_out, nor_8_out);
  not not_6 (not_6_out, Y_MN);
  assign Y_DATA_OUT = not_6_out ? {Y_O_16, Y_O_15, Y_O_14, Y_O_13, Y_O_12, Y_O_11, Y_O_10, Y_O_9, Y_O_8, Y_O_7, Y_O_6, Y_O_5, Y_O_4, Y_O_3, Y_O_2, Y_O_1} : 16'bz;  // Controlled_Buffer controlled_buffer_1
  and and_5 (and_5_out, and_1_out, and_2_out);
  and and_6 (and_6_out, and_3_out, and_4_out);
  and and_7 (FLAGS_OUT[1], and_5_out, and_6_out);
  not not_7 (FLAGS_OUT[3], F0);
  ttl74173 ttl74173_1 (
    .D1(F0), .D2(F1), .D3(F2), .D4(F3), .CLK(CLK), .RST(RST), .G1(Y_GB), .G2(Y_GB), .M(1'b0), .N(1'b0),
    .Q1(Y_O_1), .Q2(Y_O_2), .Q3(Y_O_3), .Q4(Y_O_4));
  ttl74173 ttl74173_2 (
    .D1(F4), .D2(F5), .D3(F6), .D4(F7), .CLK(CLK), .RST(RST), .G1(Y_GB), .G2(Y_GB), .M(1'b0), .N(1'b0),
    .Q1(Y_O_5), .Q2(Y_O_6), .Q3(Y_O_7), .Q4(Y_O_8));
  ttl74173 ttl74173_3 (
    .D1(F8), .D2(F9), .D3(F10), .D4(F11), .CLK(CLK), .RST(RST), .G1(Y_GB), .G2(Y_GB), .M(1'b0), .N(1'b0),
    .Q1(Y_O_9), .Q2(Y_O_10), .Q3(Y_O_11), .Q4(Y_O_12));
  ttl74173 ttl74173_4 (
    .D1(F12), .D2(F13), .D3(F14), .D4(FLAGS_OUT[2]), .CLK(CLK), .RST(RST), .G1(Y_GB), .G2(Y_GB), .M(1'b0),
    .N(1'b0), .Q1(Y_O_13), .Q2(Y_O_14), .Q3(Y_O_15), .Q4(Y_O_16));

  // Other names for the same wires on the sheet: A_EQ_B_4 = A_EQ_B[0]; A_EQ_B_3 = A_EQ_B[1]; A_EQ_B_2 = A_EQ_B[2];
  //   A_EQ_B_1 = A_EQ_B[3]; ALU_OUT[15:0] = Y_DATA_OUT; B0 = DATAIN[0]; D_IN[15:0] = DATAIN; B1 = DATAIN[1];
  //   B2 = DATAIN[2]; B3 = DATAIN[3]; B4 = DATAIN[4]; B5 = DATAIN[5]; B6 = DATAIN[6]; B7 = DATAIN[7]; B8 = DATAIN[8];
  //   B9 = DATAIN[9]; B10 = DATAIN[10]; B11 = DATAIN[11]; B12 = DATAIN[12]; B13 = DATAIN[13]; B14 = DATAIN[14];
  //   B15 = DATAIN[15]; Flags_Carry = Flags_in[0]; C_F_OUT = FLAGS_OUT[0]; Z_F_OUT = FLAGS_OUT[1]; F15 = FLAGS_OUT[2];
  //   N_F_OUT = FLAGS_OUT[2]; E_F_OUT = FLAGS_OUT[3]; S0 = S_in[0]

  // Notes on the sheet:
  //   X
  //   RES
  //   Y
endmodule

module ttl7400_gp_register (
);

  ttl74173 ttl74173_1 ();  // open: D1, D2, D3, D4, CLK, RST, G1, G2, M, N, Q1, Q2, Q3, Q4
  ttl74173 ttl74173_2 ();  // open: D1, D2, D3, D4, CLK, RST, G1, G2, M, N, Q1, Q2, Q3, Q4
  ttl74173 ttl74173_3 ();  // open: D1, D2, D3, D4, CLK, RST, G1, G2, M, N, Q1, Q2, Q3, Q4
  ttl74173 ttl74173_4 ();  // open: D1, D2, D3, D4, CLK, RST, G1, G2, M, N, Q1, Q2, Q3, Q4
endmodule

module shifter_extended (
  input  CYC_EN,
  input  SH_EN,
  input  in_3,
  input  [15:0] D_IN,
  output [15:0] out_5
);

  wire undriven_4;
  wire [15:0] undriven_2, undriven_3;
  wire [15:15] and_1_out, undriven;

  Multiplexer #(.width(16)) multiplexer_1 ();  // open: in0, in1, out, sel
  Multiplexer #(.enable("true"), .width(16)) multiplexer_2 (
    .in0({undriven[15], D_IN[15:1]}), .in1(undriven_2));  // open: out, sel, en
  and and_1 (and_1_out[15], undriven_3[0], CYC_EN);
  Demultiplexer demultiplexer_1 (.in(undriven_4));  // open: out0, out1, sel
  Multiplexer #(.width(16)) multiplexer_3 (
    .in0(undriven_3), .in1({and_1_out[15], undriven_3[15:1]}), .out(out_5), .sel(SH_EN));

  // Notes on the sheet:
  //   Maybe use some and gates instead of mux
endmodule
